// Logisim project 4 bit subtractor circuit.circ as structural Verilog: 1 circuit, main circuit main
module main (
  input  in_1,
  input  in_2,
  input  in_3,
  input  Input_Number_1,
  input  in_5,
  input  in_6,
  input  in_7,
  input  Input_Number_2,
  input  in_9,
  output out_10,
  output out_11,
  output out_12,
  output out_13,
  output Overflow
);

  wire and_1_out, and_2_out, and_3_out, and_4_out, and_5_out, and_6_out, and_7_out, and_8_out, not_1_out,
       not_2_out, not_3_out, not_4_out, or_1_out, or_2_out, or_3_out, xor_1_out, xor_2_out, xor_3_out,
       xor_4_out;

  not not_1 (not_1_out, in_7);
  not not_2 (not_2_out, Input_Number_2);
  not not_3 (not_3_out, in_2);
  not not_4 (not_4_out, in_9);
  xor xor_1 (xor_1_out, not_3_out, in_6);
  xor xor_2 (xor_2_out, not_4_out, in_5);
  xor xor_3 (xor_3_out, not_2_out, Input_Number_1);
  xor xor_4 (xor_4_out, not_1_out, in_3);
  xor xor_5 (out_13, xor_1_out, in_1);
  xor xor_6 (out_12, xor_2_out, or_1_out);
  xor xor_7 (out_11, xor_3_out, or_2_out);
  xor xor_8 (out_10, xor_4_out, or_3_out);
  and and_1 (and_1_out, in_1, xor_1_out);
  and and_2 (and_2_out, in_6, not_3_out);
  and and_3 (and_3_out, or_1_out, xor_2_out);
  and and_4 (and_4_out, in_5, not_4_out);
  and and_5 (and_5_out, or_2_out, xor_3_out);
  and and_6 (and_6_out, Input_Number_1, not_2_out);
  and and_7 (and_7_out, or_3_out, xor_4_out);
  and and_8 (and_8_out, in_3, not_1_out);
  or or_1 (or_1_out, and_1_out, and_2_out);
  or or_2 (or_2_out, and_3_out, and_4_out);
  or or_3 (or_3_out, and_5_out, and_6_out);
  or or_4 (Overflow, and_7_out, and_8_out);

  // Notes on the sheet:
  //   Carry in of 1 will add 1 to the number 
  //   to 2's complement
  //   which along with the inverters will convert
  //   4 Bit Subtractor Circuit
  //   Output Number
  //   Carry Bit
  //   Carry Bit
  //   Carry Bit
endmodule
