// Logisim project 4 bit ALU with Registers circuit.circ as structural Verilog: 1 circuit, main circuit main
module main (
  input  in_1,
  input  in_2,
  input  in_3,
  input  in_4,
  input  in_5,
  input  [1:0] in_6,
  input  in_7,
  input  in_8,
  input  in_9,
  input  in_10,
  input  in_11,
  output [3:0] out_12
);

  wire nand_1_out, nand_2_out, nand_3_out, nand_4_out, nand_5_out, nand_6_out, nand_7_out, nand_8_out,
       nand_9_out, nand_10_out, nand_11_out, nand_12_out, nand_13_out, nand_14_out, nand_15_out, nand_16_out,
       nand_18_out, nand_20_out, nand_22_out, nand_24_out, nand_26_out, nand_28_out, nand_30_out,
       nand_32_out, not_1_out, not_2_out, not_3_out, not_4_out, not_5_out, not_6_out, not_7_out, not_8_out;
  wire [3:0] adder_1_out, and_1_out, nand_17_out, nand_25_out, or_1_out, subtractor_1_out;

  not not_1 (not_1_out, in_2);
  not not_2 (not_2_out, in_4);
  not not_3 (not_3_out, in_5);
  not not_4 (not_4_out, in_7);
  not not_5 (not_5_out, in_8);
  not not_6 (not_6_out, in_10);
  not not_7 (not_7_out, in_11);
  not not_8 (not_8_out, in_1);
  nand nand_1 (nand_1_out, in_1, in_3);
  nand nand_2 (nand_2_out, in_3, not_8_out);
  nand nand_3 (nand_3_out, in_2, in_3);
  nand nand_4 (nand_4_out, in_3, not_1_out);
  nand nand_5 (nand_5_out, in_4, in_3);
  nand nand_6 (nand_6_out, in_3, not_2_out);
  nand nand_7 (nand_7_out, in_5, in_3);
  nand nand_8 (nand_8_out, in_3, not_3_out);
  nand nand_9 (nand_9_out, in_7, in_9);
  nand nand_10 (nand_10_out, in_9, not_4_out);
  nand nand_11 (nand_11_out, in_8, in_9);
  nand nand_12 (nand_12_out, in_9, not_5_out);
  nand nand_13 (nand_13_out, in_10, in_9);
  nand nand_14 (nand_14_out, in_9, not_6_out);
  nand nand_15 (nand_15_out, in_11, in_9);
  nand nand_16 (nand_16_out, in_9, not_7_out);
  nand nand_17 (nand_17_out[0], nand_1_out, nand_18_out);
  nand nand_18 (nand_18_out, nand_17_out[0], nand_2_out);
  nand nand_19 (nand_17_out[1], nand_3_out, nand_20_out);
  nand nand_20 (nand_20_out, nand_17_out[1], nand_4_out);
  nand nand_21 (nand_17_out[2], nand_5_out, nand_22_out);
  nand nand_22 (nand_22_out, nand_17_out[2], nand_6_out);
  nand nand_23 (nand_17_out[3], nand_7_out, nand_24_out);
  nand nand_24 (nand_24_out, nand_17_out[3], nand_8_out);
  nand nand_25 (nand_25_out[0], nand_9_out, nand_26_out);
  nand nand_26 (nand_26_out, nand_25_out[0], nand_10_out);
  nand nand_27 (nand_25_out[1], nand_11_out, nand_28_out);
  nand nand_28 (nand_28_out, nand_25_out[1], nand_12_out);
  nand nand_29 (nand_25_out[2], nand_13_out, nand_30_out);
  nand nand_30 (nand_30_out, nand_25_out[2], nand_14_out);
  nand nand_31 (nand_25_out[3], nand_15_out, nand_32_out);
  nand nand_32 (nand_32_out, nand_25_out[3], nand_16_out);
  Adder #(.width(4)) adder_1 (.a(nand_17_out), .b(nand_25_out), .out(adder_1_out));  // open: cin, cout
  Subtractor #(.width(4)) subtractor_1 (.a(nand_17_out), .b(nand_25_out), .out(subtractor_1_out));  // open: bin, bout
  assign and_1_out = nand_17_out & nand_25_out;  // AND_Gate and_1, 4 bits wide
  assign or_1_out = nand_17_out | nand_25_out;  // OR_Gate or_1, 4 bits wide
  Multiplexer #(.select(2), .width(4), .enable("false")) multiplexer_1 (
    .in0(adder_1_out), .in1(subtractor_1_out), .in2(and_1_out), .in3(or_1_out), .out(out_12), .sel(in_6));

  // Notes on the sheet:
  //   4 bit register input
  //   4 bit register input
  //   Memory Enable Tied to Clock
  //   Memory Enable Tied to Clock
  //   Register Stored
  //   4 bit ALU
endmodule
