// Logisim project 4 bit register circuit.circ as structural Verilog: 1 circuit, main circuit main
module main (
  input  in_1,
  input  in_2,
  input  in_3,
  input  in_4,
  input  in_5,
  output Register_Stored,
  output out_7,
  output out_8,
  output out_9
);

  wire nand_1_out, nand_2_out, nand_3_out, nand_4_out, nand_5_out, nand_6_out, nand_7_out, nand_8_out,
       nand_10_out, nand_12_out, nand_14_out, nand_16_out, not_1_out, not_2_out, not_3_out, not_4_out;

  not not_1 (not_1_out, in_1);
  not not_2 (not_2_out, in_2);
  not not_3 (not_3_out, in_4);
  not not_4 (not_4_out, in_5);
  nand nand_1 (nand_1_out, in_1, in_3);
  nand nand_2 (nand_2_out, in_3, not_1_out);
  nand nand_3 (nand_3_out, in_2, in_3);
  nand nand_4 (nand_4_out, in_3, not_2_out);
  nand nand_5 (nand_5_out, in_4, in_3);
  nand nand_6 (nand_6_out, in_3, not_3_out);
  nand nand_7 (nand_7_out, in_5, in_3);
  nand nand_8 (nand_8_out, in_3, not_4_out);
  nand nand_9 (out_7, nand_3_out, nand_10_out);
  nand nand_10 (nand_10_out, out_7, nand_4_out);
  nand nand_11 (out_8, nand_5_out, nand_12_out);
  nand nand_12 (nand_12_out, out_8, nand_6_out);
  nand nand_13 (out_9, nand_7_out, nand_14_out);
  nand nand_14 (nand_14_out, out_9, nand_8_out);
  nand nand_15 (Register_Stored, nand_1_out, nand_16_out);
  nand nand_16 (nand_16_out, Register_Stored, nand_2_out);

  // Notes on the sheet:
  //   4 bit register input
  //   Memory Enable Tied to Clock
endmodule
